# Fritzing sketch ConnectionDiagram (saved by Fritzing 0.9.2b)

parts:
  S2 = Round Pushbutton
  S3 = Round Pushbutton
  S4 = Round Pushbutton
  J1 = Piezo Speaker
  Q1 = TRANSISTOR_PNP [package=to-92]
  10K = Resistor [tolerance=±5% resistance=220 package=THT]
  JP1 = Header 4 [package=screwterminal-3.5mm-4_lock]
  J2 = Screw terminal - 2 pins [package=THT]

nets:
  N1: S2.leg0, JP1.1
  N2: S2.leg1, S3.leg1, S4.leg1, J1.pin1, JP1.4
  N3: S3.leg0, JP1.3
  N4: S4.leg0, JP1.2
  N5: Q1.C, J2.pin1
  N6: 10K.Pin_1, J2.pin2

notes:
  Feather Board
  3.3v
  Pin 5
  Feather Board
  Pin 10
  Pin 11
  Pin 12
  GND
  Keys
  Buzzer
  PNP Transistor
